// Logisim project control_logic.circ as structural Verilog: 1 circuit, main circuit control_logic
module control_logic (
  input  [31:0] inst,
  input  BrEq,
  input  BrLt,
  output PCSel,
  output RegWEn,
  output [2:0] ImmSel,
  output BrUn,
  output ASel,
  output BSel,
  output [3:0] ALUSel,
  output MemRW,
  output [1:0] WBSel,
  output CSRSel,
  output CSRWen
);

  wire and_1_out, and_2_out, and_3_out, and_4_out, and_5_out, and_6_out, and_7_out, and_8_out, and_9_out,
       and_10_out, and_11_out, and_12_out, and_13_out, and_14_out, and_15_out, and_16_out, and_17_out,
       and_18_out, and_19_out, and_20_out, comparator_1_eq, comparator_2_eq, comparator_3_eq,
       comparator_4_eq, comparator_5_eq, comparator_6_eq, comparator_7_eq, comparator_8_eq, comparator_9_eq,
       comparator_10_eq, comparator_11_eq, comparator_12_eq, comparator_13_eq, comparator_14_eq,
       comparator_15_eq, comparator_16_eq, comparator_17_eq, comparator_18_eq, comparator_19_eq,
       comparator_20_eq, comparator_21_eq, comparator_22_eq, comparator_23_eq, comparator_24_eq,
       comparator_25_eq, comparator_26_eq, comparator_27_eq, comparator_28_eq, comparator_29_eq,
       comparator_30_eq, comparator_31_eq, comparator_32_eq, comparator_33_eq, comparator_34_eq,
       comparator_35_eq, comparator_36_eq, comparator_37_eq, comparator_38_eq, comparator_39_eq,
       comparator_40_eq, comparator_42_eq, comparator_43_eq, comparator_45_eq, comparator_46_eq, not_1_out,
       not_2_out, not_3_out, or_1_out, or_2_out, or_3_out;
  wire [3:0] multiplexer_1_out, multiplexer_13_out, multiplexer_14_out, multiplexer_15_out, rom_2_data;

  ROM #(.addrWidth(7), .dataWidth(3), .misaligned("true")) rom_1 (.addr(inst[6:0]), .data(ImmSel));
  ROM #(.addrWidth(3), .dataWidth(4)) rom_2 (.addr(inst[14:12]), .data(rom_2_data));
  Comparator #(.width(3)) comparator_1 (.a(inst[14:12]), .b(3'b000), .eq(comparator_1_eq));  // open: gt, lt
  Comparator #(.width(7)) comparator_2 (.a(inst[31:25]), .b({7{1'b0}}), .eq(comparator_2_eq));  // open: gt, lt
  Comparator #(.width(3)) comparator_3 (.a(inst[14:12]), .b(3'b000), .eq(comparator_3_eq));  // open: gt, lt
  Comparator #(.width(7)) comparator_4 (.a(inst[31:25]), .b(7'b0000001), .eq(comparator_4_eq));  // open: gt, lt
  Comparator #(.width(3)) comparator_5 (.a(inst[14:12]), .b(3'b000), .eq(comparator_5_eq));  // open: gt, lt
  Comparator #(.width(7)) comparator_6 (.a(inst[31:25]), .b(7'b0100000), .eq(comparator_6_eq));  // open: gt, lt
  Comparator #(.width(3)) comparator_7 (.a(inst[14:12]), .b(3'b001), .eq(comparator_7_eq));  // open: gt, lt
  Comparator #(.width(7)) comparator_8 (.a(inst[31:25]), .b({7{1'b0}}), .eq(comparator_8_eq));  // open: gt, lt
  Comparator #(.width(3)) comparator_9 (.a(inst[14:12]), .b(3'b001), .eq(comparator_9_eq));  // open: gt, lt
  Comparator #(.width(7)) comparator_10 (.a(inst[31:25]), .b(7'b0000001), .eq(comparator_10_eq));  // open: gt, lt
  Comparator #(.width(3)) comparator_11 (.a(inst[14:12]), .b(3'b010), .eq(comparator_11_eq));  // open: gt, lt
  Comparator #(.width(7)) comparator_12 (.a(inst[31:25]), .b({7{1'b0}}), .eq(comparator_12_eq));  // open: gt, lt
  Comparator #(.width(3)) comparator_13 (.a(inst[14:12]), .b(3'b011), .eq(comparator_13_eq));  // open: gt, lt
  Comparator #(.width(7)) comparator_14 (.a(inst[31:25]), .b(7'b0000001), .eq(comparator_14_eq));  // open: gt, lt
  Comparator #(.width(3)) comparator_15 (.a(inst[14:12]), .b(3'b100), .eq(comparator_15_eq));  // open: gt, lt
  Comparator #(.width(7)) comparator_16 (.a(inst[31:25]), .b({7{1'b0}}), .eq(comparator_16_eq));  // open: gt, lt
  Comparator #(.width(3)) comparator_17 (.a(inst[14:12]), .b(3'b101), .eq(comparator_17_eq));  // open: gt, lt
  Comparator #(.width(7)) comparator_18 (.a(inst[31:25]), .b({7{1'b0}}), .eq(comparator_18_eq));  // open: gt, lt
  Comparator #(.width(3)) comparator_19 (.a(inst[14:12]), .b(3'b101), .eq(comparator_19_eq));  // open: gt, lt
  Comparator #(.width(7)) comparator_20 (.a(inst[31:25]), .b(7'b0100000), .eq(comparator_20_eq));  // open: gt, lt
  Comparator #(.width(3)) comparator_21 (.a(inst[14:12]), .b(3'b110), .eq(comparator_21_eq));  // open: gt, lt
  Comparator #(.width(7)) comparator_22 (.a(inst[31:25]), .b({7{1'b0}}), .eq(comparator_22_eq));  // open: gt, lt
  Comparator #(.width(3)) comparator_23 (.a(inst[14:12]), .b(3'b111), .eq(comparator_23_eq));  // open: gt, lt
  Comparator #(.width(7)) comparator_24 (.a(inst[31:25]), .b({7{1'b0}}), .eq(comparator_24_eq));  // open: gt, lt
  and and_1 (and_1_out, comparator_1_eq, comparator_2_eq);
  and and_2 (and_2_out, comparator_3_eq, comparator_4_eq);
  and and_3 (and_3_out, comparator_5_eq, comparator_6_eq);
  and and_4 (and_4_out, comparator_7_eq, comparator_8_eq);
  and and_5 (and_5_out, comparator_9_eq, comparator_10_eq);
  and and_6 (and_6_out, comparator_11_eq, comparator_12_eq);
  and and_7 (and_7_out, comparator_13_eq, comparator_14_eq);
  and and_8 (and_8_out, comparator_15_eq, comparator_16_eq);
  and and_9 (and_9_out, comparator_17_eq, comparator_18_eq);
  and and_10 (and_10_out, comparator_19_eq, comparator_20_eq);
  and and_11 (and_11_out, comparator_21_eq, comparator_22_eq);
  and and_12 (and_12_out, comparator_23_eq, comparator_24_eq);
  Comparator #(.width(3)) comparator_25 (.a(inst[14:12]), .b(3'b101), .eq(comparator_25_eq));  // open: gt, lt
  Comparator #(.width(7)) comparator_26 (.a(inst[31:25]), .b(7'b0100000), .eq(comparator_26_eq));  // open: gt, lt
  Multiplexer #(.enable("false"), .width(4)) multiplexer_1 (
    .in1(4'b0000), .out(multiplexer_1_out), .sel(and_1_out));  // open: in0
  Multiplexer #(.enable("false"), .width(4)) multiplexer_2 (
    .in1(4'b1010), .out(multiplexer_1_out), .sel(and_2_out));  // open: in0
  Multiplexer #(.enable("false"), .width(4)) multiplexer_3 (
    .in1(4'b1100), .out(multiplexer_1_out), .sel(and_3_out));  // open: in0
  Multiplexer #(.enable("false"), .width(4)) multiplexer_4 (
    .in1(4'b0110), .out(multiplexer_1_out), .sel(and_4_out));  // open: in0
  Multiplexer #(.enable("false"), .width(4)) multiplexer_5 (
    .in1(4'b1110), .out(multiplexer_1_out), .sel(and_5_out));  // open: in0
  Multiplexer #(.enable("false"), .width(4)) multiplexer_6 (
    .in1(4'b0111), .out(multiplexer_1_out), .sel(and_6_out));  // open: in0
  Multiplexer #(.enable("false"), .width(4)) multiplexer_7 (
    .in1(4'b1011), .out(multiplexer_1_out), .sel(and_7_out));  // open: in0
  Multiplexer #(.enable("false"), .width(4)) multiplexer_8 (
    .in1(4'b0011), .out(multiplexer_1_out), .sel(and_8_out));  // open: in0
  Multiplexer #(.enable("false"), .width(4)) multiplexer_9 (
    .in1(4'b0100), .out(multiplexer_1_out), .sel(and_9_out));  // open: in0
  Multiplexer #(.enable("false"), .width(4)) multiplexer_10 (
    .in1(4'b0101), .out(multiplexer_1_out), .sel(and_10_out));  // open: in0
  Multiplexer #(.enable("false"), .width(4)) multiplexer_11 (
    .in1(4'b0010), .out(multiplexer_1_out), .sel(and_11_out));  // open: in0
  Multiplexer #(.enable("false"), .width(4)) multiplexer_12 (
    .in1(4'b0001), .out(multiplexer_1_out), .sel(and_12_out));  // open: in0
  and and_13 (and_13_out, comparator_25_eq, comparator_26_eq);
  Multiplexer #(.enable("false"), .width(4)) multiplexer_13 (
    .in0(rom_2_data), .in1(4'b0101), .out(multiplexer_13_out), .sel(and_13_out));
  Comparator #(.width(7)) comparator_27 (.a(inst[6:0]), .b(7'b0010011), .eq(comparator_27_eq));  // open: gt, lt
  Comparator #(.width(7)) comparator_28 (.a(inst[6:0]), .b(7'b0110011), .eq(comparator_28_eq));  // open: gt, lt
  or or_1 (or_1_out, comparator_27_eq, comparator_28_eq);
  Comparator #(.width(7)) comparator_29 (.a(inst[6:0]), .b(7'b0110011), .eq(comparator_29_eq));  // open: gt, lt
  Multiplexer #(.enable("false"), .width(4)) multiplexer_14 (
    .in0(multiplexer_13_out), .in1(multiplexer_1_out), .out(multiplexer_14_out), .sel(comparator_29_eq));
  Multiplexer #(.enable("false"), .width(4)) multiplexer_15 (
    .in0(4'b0000), .in1(multiplexer_14_out), .out(multiplexer_15_out), .sel(or_1_out));
  Comparator #(.width(7)) comparator_30 (.a(inst[6:0]), .b(7'b1100011), .eq(comparator_30_eq));  // open: gt, lt
  Comparator #(.width(3)) comparator_31 (.a(inst[14:12]), .b(3'b000), .eq(comparator_31_eq));  // open: gt, lt
  Comparator #(.width(3)) comparator_32 (.a(inst[14:12]), .b(3'b001), .eq(comparator_32_eq));  // open: gt, lt
  not not_1 (not_1_out, BrEq);
  Comparator #(.width(3)) comparator_33 (.a(inst[14:12]), .b(3'b100), .eq(comparator_33_eq));  // open: gt, lt
  Comparator #(.width(3)) comparator_34 (.a(inst[14:12]), .b(3'b101), .eq(comparator_34_eq));  // open: gt, lt
  not not_2 (not_2_out, BrLt);
  Comparator #(.mode("unsigned"), .width(3)) comparator_35 (
    .a(inst[14:12]), .b(3'b110), .eq(comparator_35_eq));  // open: gt, lt
  Comparator #(.mode("unsigned"), .width(3)) comparator_36 (
    .a(inst[14:12]), .b(3'b111), .eq(comparator_36_eq));  // open: gt, lt
  not not_3 (not_3_out, BrLt);
  Multiplexer #(.enable("false"), .width(4)) multiplexer_16 (
    .in0(multiplexer_15_out), .in1(4'b1101), .out(ALUSel), .sel(comparator_37_eq));
  Comparator #(.width(7)) comparator_37 (.a(inst[6:0]), .b(7'b0110111), .eq(comparator_37_eq));  // open: gt, lt
  Comparator #(.width(7)) comparator_38 (.a(inst[6:0]), .b(7'b0100011), .eq(comparator_38_eq));  // open: gt, lt
  Comparator #(.width(7)) comparator_39 (.a(inst[6:0]), .b(7'b1100011), .eq(comparator_39_eq));  // open: gt, lt
  Comparator #(.width(7)) comparator_40 (.a(inst[6:0]), .b(7'b1110011), .eq(comparator_40_eq));  // open: gt, lt
  Comparator #(.width(7)) comparator_41 (.a(inst[6:0]), .b(7'b0100011), .eq(MemRW));  // open: gt, lt
  and and_14 (and_14_out, comparator_31_eq, BrEq);
  and and_15 (and_15_out, comparator_32_eq, not_1_out);
  and and_16 (and_16_out, comparator_33_eq, BrLt);
  and and_17 (and_17_out, comparator_34_eq, not_2_out);
  and and_18 (and_18_out, comparator_35_eq, BrLt);
  and and_19 (and_19_out, comparator_36_eq, not_3_out);
  or or_2 (or_2_out, comparator_38_eq, comparator_39_eq, comparator_40_eq);
  not not_4 (RegWEn, or_2_out);
  or or_3 (or_3_out, and_14_out, and_15_out, and_16_out, and_17_out, and_18_out, and_19_out);
  Comparator #(.width(7)) comparator_42 (.a(inst[6:0]), .b(7'b1110011), .eq(comparator_42_eq));  // open: gt, lt
  Comparator #(.width(3)) comparator_43 (.a(inst[14:12]), .b(3'b101), .eq(comparator_43_eq));  // open: gt, lt
  Comparator #(.width(7)) comparator_44 (.a(inst[6:0]), .b(7'b1110011), .eq(CSRWen));  // open: gt, lt
  and and_20 (and_20_out, comparator_30_eq, or_3_out);
  Comparator #(.width(7)) comparator_45 (.a(inst[6:0]), .b(7'b1100111), .eq(comparator_45_eq));  // open: gt, lt
  Comparator #(.width(7)) comparator_46 (.a(inst[6:0]), .b(7'b1101111), .eq(comparator_46_eq));  // open: gt, lt
  and and_21 (CSRSel, comparator_42_eq, comparator_43_eq);
  ROM #(.addrWidth(7), .dataWidth(2)) rom_3 (.addr(inst[6:0]), .data(WBSel));
  ROM #(.addrWidth(7), .dataWidth(1)) rom_4 (.addr(inst[6:0]));  // open: data
  ROM #(.addrWidth(7), .dataWidth(1)) rom_5 (.addr(inst[6:0]));  // open: data
  or or_4 (PCSel, and_20_out, comparator_45_eq, comparator_46_eq);

  assign BrUn = inst[13];

  // Other names for the same wires on the sheet: opcode[6:0] = inst[6:0]; funct3[2:0] = inst[14:12];
  //   funct7[6:0] = inst[31:25]

  // Notes on the sheet:
  //   contents of rom_1 (hex, n*v repeats v):
  //   23*0 3 11*0 1 19*0 3 43*0 2 11*0 4
  //   contents of rom_2 (hex, n*v repeats v):
  //   0 6 7 5 3 4 2 1
  //   INPUTS to your circuit
  //   DON'T CHANGE THE LOCATIONS OF THE INPUTS AND OUTPUTS!
  //   OUTPUT from your circuit
  //   contents of rom_3 (hex, n*v repeats v):
  //   19*0 1 0 0 0 1 27*0 1 0 0 0 1 47*0 2 7*0 2
  //   contents of rom_4 (hex, n*v repeats v):
  //   23*0 1 31*0 1 43*0 1 11*0 1
  //   contents of rom_5 (hex, n*v repeats v):
  //   0 0 0 1 15*0 1 0 0 0 1 11*0 1 19*0 1 43*0 1 0 0 0 1 7*0 1
endmodule
