// Logisim project cpu.circ as structural Verilog: 1 circuit, main circuit cpu
module cpu (
  input  clk,
  input  [31:0] INSTRUCTION,
  input  [31:0] READ_DATA,
  output [31:0] WRITE_ADDRESS,
  output [31:0] PROGRAM_COUNTER,
  output [31:0] ra,
  output [31:0] sp,
  output [31:0] t0,
  output [31:0] t1,
  output [31:0] t2,
  output [31:0] s0,
  output [31:0] s1,
  output [31:0] a0,
  output [31:0] tohost,
  output [3:0] WRITE_ENABLE,
  output [31:0] WRITE_DATA
);

  wire AorPc, BorImm, BrEq, BrLt, comparator_1_eq, control_logic_1_brun, CSRSel, CSRWen, MemRW, PcSel, RegWEn;
  wire [1:0] bit_extender_4_out, bit_extender_9_out, bit_extender_12_out, MemALUPc;
  wire [2:0] ImmSel;
  wire [3:0] ALUSel, rom_1_data;
  wire [7:0] bit_extender_2_out;
  wire [15:0] bit_extender_3_out;
  wire [31:0] adder_1_out, adder_2_out, bit_extender_1_out, bit_extender_5_out, bit_extender_6_out,
       bit_extender_7_out, bit_extender_8_out, bit_extender_10_out, bit_extender_11_out, Imm, INS,
       multiplexer_1_out, multiplexer_2_out, multiplexer_3_out, multiplexer_4_out, multiplexer_5_out,
       multiplexer_8_out, multiplexer_10_out, PC, RD1, RD2, READ_DATA2, WD;

  Multiplexer #(.enable("false"), .width(32)) multiplexer_1 (
    .in0(adder_1_out), .in1(WRITE_ADDRESS), .out(multiplexer_1_out), .sel(PcSel));
  Adder #(.width(32)) adder_1 (.a(PROGRAM_COUNTER), .b(32'h4), .out(adder_1_out));  // open: cin, cout
  Register #(.width(32)) u_PC (.D(multiplexer_1_out), .clk(clk), .Q(PROGRAM_COUNTER));  // open: en, clr
  Register #(.width(32)) register_1 (.D(multiplexer_2_out), .clk(clk), .Q(INS));  // open: en, clr
  Multiplexer #(.enable("false"), .width(32)) multiplexer_2 (
    .in0(INSTRUCTION), .in1(32'h13), .out(multiplexer_2_out), .sel(PcSel));
  Register #(.width(32)) register_2 (.D(PROGRAM_COUNTER), .clk(clk), .Q(PC));  // open: en, clr
  control_logic control_logic_1 (
    .CSRWen(CSRWen), .PCSel(PcSel), .RegWEn(RegWEn), .ImmSel(ImmSel), .BrUn(control_logic_1_brun),
    .ASel(AorPc), .BSel(BorImm), .ALUSel(ALUSel), .MemRW(MemRW), .WBSel(MemALUPc), .CSRSel(CSRSel),
    .inst(INS), .BrEq(BrEq), .BrLt(BrLt));
  imm_gen imm_gen_1 (.inst(INS), .ImmSel(ImmSel), .imm(Imm));
  regfile regfile_1 (
    .rs1(INS[19:15]), .rs2(INS[24:20]), .rd(INS[11:7]), .Write_Data(WD), .RegWEn(RegWEn), .clk(clk), .ra(ra),
    .sp(sp), .t0(t0), .t1(t1), .t2(t2), .s0(s0), .s1(s1), .a0(a0), .Read_Data_1(RD1), .Read_Data_2(RD2));
  branch_comp branch_comp_1 (.rs1(RD1), .rs2(RD2), .BrUn(control_logic_1_brun), .BrEq(BrEq), .BrLt(BrLt));
  assign bit_extender_1_out = {{27{1'b0}}, INS[19:15]};  // Bit_Extender bit_extender_1
  Multiplexer #(.enable("false"), .width(32)) multiplexer_3 (
    .in0(RD2), .in1(Imm), .out(multiplexer_3_out), .sel(BorImm));
  Multiplexer #(.enable("false"), .width(32)) multiplexer_4 (.in0(RD1), .in1(PC), .out(multiplexer_4_out), .sel(AorPc));
  Multiplexer #(.enable("false"), .width(32)) multiplexer_5 (
    .in0(RD1), .in1(bit_extender_1_out), .out(multiplexer_5_out), .sel(CSRSel));
  alu alu_1 (.Result(WRITE_ADDRESS), .A(multiplexer_4_out), .B(multiplexer_3_out), .ALUSel(ALUSel));
  Adder #(.width(32)) adder_2 (.a(PC), .b(32'h4), .out(adder_2_out));  // open: cin, cout
  csr csr_1 (.CSR_address(INS[31:20]), .CSR_din(multiplexer_5_out), .CSR_WE(CSRWen), .clk(clk), .tohost(tohost));
  Multiplexer #(.enable("false"), .select(2), .width(32)) multiplexer_6 (
    .in0(READ_DATA2), .in1(WRITE_ADDRESS), .in2(adder_2_out), .out(WD), .sel(MemALUPc));  // open: in3
  Bit_Extender #(.in_width(32), .out_width(8)) bit_extender_2 (.in(RD2), .out(bit_extender_2_out));
  Bit_Extender #(.in_width(32)) bit_extender_3 (.in(RD2), .out(bit_extender_3_out));
  Bit_Extender #(.in_width(32), .out_width(2)) bit_extender_4 (.in(WRITE_ADDRESS), .out(bit_extender_4_out));
  assign bit_extender_5_out = {{24{READ_DATA[7]}}, READ_DATA[7:0]};  // Bit_Extender bit_extender_5
  assign bit_extender_6_out = {{24{READ_DATA[15]}}, READ_DATA[15:8]};  // Bit_Extender bit_extender_6
  assign bit_extender_7_out = {{24{READ_DATA[23]}}, READ_DATA[23:16]};  // Bit_Extender bit_extender_7
  assign bit_extender_8_out = {{24{READ_DATA[31]}}, READ_DATA[31:24]};  // Bit_Extender bit_extender_8
  Bit_Extender #(.in_width(32), .out_width(2)) bit_extender_9 (.in(WRITE_ADDRESS), .out(bit_extender_9_out));
  assign bit_extender_10_out = {{16{READ_DATA[15]}}, READ_DATA[15:0]};  // Bit_Extender bit_extender_10
  assign bit_extender_11_out = {{16{READ_DATA[31]}}, READ_DATA[31:16]};  // Bit_Extender bit_extender_11
  Comparator #(.width(7)) comparator_1 (.a(7'b0100011), .b(INS[6:0]), .eq(comparator_1_eq));  // open: gt, lt
  ROM #(.addrWidth(5), .dataWidth(4)) rom_1 (.addr({bit_extender_4_out, INS[14:12]}), .data(rom_1_data));
  Multiplexer #(.enable("false"), .select(3), .width(32)) multiplexer_7 (
    .in0({bit_extender_2_out, bit_extender_2_out, bit_extender_2_out, bit_extender_2_out}),
    .in1({bit_extender_3_out, bit_extender_3_out}), .in2(RD2), .out(WRITE_DATA), .sel(INS[14:12]));  // open: in3, in4, in5, in6, in7
  Multiplexer #(.enable("false"), .select(2), .width(32)) multiplexer_8 (
    .in0(bit_extender_5_out), .in1(bit_extender_6_out), .in2(bit_extender_7_out), .in3(bit_extender_8_out),
    .out(multiplexer_8_out), .sel(bit_extender_9_out));
  Bit_Extender #(.in_width(32), .out_width(2)) bit_extender_12 (.in(WRITE_ADDRESS), .out(bit_extender_12_out));
  Multiplexer #(.enable("false"), .width(4)) multiplexer_9 (
    .in0(4'b0000), .in1(rom_1_data), .out(WRITE_ENABLE), .sel(comparator_1_eq));
  Multiplexer #(.enable("false"), .select(2), .width(32)) multiplexer_10 (
    .in0(bit_extender_10_out), .in1(bit_extender_10_out), .in2(bit_extender_11_out),
    .in3(bit_extender_11_out), .out(multiplexer_10_out), .sel(bit_extender_12_out));
  Multiplexer #(.enable("false"), .select(3), .width(32)) multiplexer_11 (
    .in0(multiplexer_8_out), .in1(multiplexer_10_out), .in2(READ_DATA), .out(READ_DATA2), .sel(INS[14:12]));  // open: in3, in4, in5, in6, in7

  // Other names for the same wires on the sheet: rs1[4:0] = INS[19:15]; rs2[4:0] = INS[24:20];
  //   Result[31:0] = WRITE_ADDRESS

  // Notes on the sheet:
  //   Output to IMEM
  //   IMEM (do **NOT** move this)
  //   Inputs from IMEM
  //   It is OK to move the PC, RegFile, ALU, MEM, Branch Comp, Imm Gen, and Control Logic to wherever is most convenient for you when constructing your CPU, and to delete this text
  //   Inputs/Outputs for testing. Do **NOT** move these.
  //   Outputs To DMEM
  //   DMEM (do **NOT** move this)
  //   contents of rom_1 (hex, n*v repeats v):
  //   1 3 f 5*0 2 6 f 5*0 4 c f 5*0 8 c f
  //   Inputs From DMEM
endmodule
