// Logisim project imm_gen.circ as structural Verilog: 1 circuit, main circuit imm_gen
module imm_gen (
  input  [31:0] inst,
  input  [2:0] ImmSel,
  output [31:0] imm
);

  wire [31:0] J;

  assign J = {{11{inst[31]}}, {inst[31], inst[19:12], inst[20], inst[30:21], 1'b0}};  // Bit_Extender bit_extender_1
  Multiplexer #(.enable("false"), .select(3), .width(32)) multiplexer_1 (
    .in0({{21{inst[31]}}, inst[30:20]}), .in1({{21{inst[31]}}, inst[30:25], inst[11:7]}),
    .in2({{20{inst[31]}}, inst[7], inst[30:25], inst[11:8], 1'b0}), .in3({inst[31:12], {12{1'b0}}}), .in4(J),
    .out(imm), .sel(ImmSel));  // open: in5, in6, in7

  // Other names for the same wires on the sheet: B[31:1] = {{20{inst[31]}}, inst[7], inst[30:25], inst[11:8]};
  //   Bshit[12:1] = {inst[31], inst[7], inst[30:25], inst[11:8]}; i117[4:0] = inst[11:7];
  //   S[31:0] = {{21{inst[31]}}, inst[30:25], inst[11:7]}; i1912[7:0] = inst[19:12]; U[31:12] = inst[31:12];
  //   I[31:0] = {{21{inst[31]}}, inst[30:20]}; i2420[4:0] = inst[24:20]; i3125[6:0] = inst[31:25]

  // Notes on the sheet:
  //   INPUTS to your circuit
  //   DON'T CHANGE THE LOCATIONS OF THE INPUTS AND OUTPUTS!
  //   OUTPUT from your circuit
endmodule
