// Logisim project regfile.circ as structural Verilog: 1 circuit, main circuit regfile
module regfile (
  input  [4:0] rs1,
  input  [4:0] rs2,
  input  [4:0] rd,
  input  [31:0] Write_Data,
  input  RegWEn,
  input  clk,
  output [31:0] ra,
  output [31:0] sp,
  output [31:0] t0,
  output [31:0] t1,
  output [31:0] t2,
  output [31:0] s0,
  output [31:0] s1,
  output [31:0] a0,
  output [31:0] Read_Data_1,
  output [31:0] Read_Data_2
);

  wire x1, x2, x3, x4, x5, x6, x7, x8, x9, x10, x11, x12, x13, x14, x15, x16, x17, x18, x19, x20, x21, x22,
       x23, x24, x25, x26, x27, x28, x29, x30, x31;
  wire [31:0] o0, o3, o4, o11, o12, o13, o14, o15, o16, o17, o18, o19, o20, o21, o22, o23, o24, o25, o26,
       o27, o28, o29, o30, o31;

  Register #(.width(32)) register_1 (.Q(o0));  // open: D, en, clk, clr
  Register #(.width(32)) register_2 (.D(Write_Data), .en(x1), .clk(clk), .Q(ra));  // open: clr
  Register #(.width(32)) register_3 (.D(Write_Data), .en(x2), .clk(clk), .Q(sp));  // open: clr
  Register #(.width(32)) register_4 (.D(Write_Data), .en(x3), .clk(clk), .Q(o3));  // open: clr
  Register #(.width(32)) register_5 (.D(Write_Data), .en(x4), .clk(clk), .Q(o4));  // open: clr
  Register #(.width(32)) register_6 (.D(Write_Data), .en(x5), .clk(clk), .Q(t0));  // open: clr
  Register #(.width(32)) register_7 (.D(Write_Data), .en(x6), .clk(clk), .Q(t1));  // open: clr
  Register #(.width(32)) register_8 (.D(Write_Data), .en(x7), .clk(clk), .Q(t2));  // open: clr
  Register #(.width(32)) register_9 (.D(Write_Data), .en(x8), .clk(clk), .Q(s0));  // open: clr
  Register #(.width(32)) register_10 (.D(Write_Data), .en(x9), .clk(clk), .Q(s1));  // open: clr
  Register #(.width(32)) register_11 (.D(Write_Data), .en(x10), .clk(clk), .Q(a0));  // open: clr
  Register #(.width(32)) register_12 (.D(Write_Data), .en(x11), .clk(clk), .Q(o11));  // open: clr
  Register #(.width(32)) register_13 (.D(Write_Data), .en(x12), .clk(clk), .Q(o12));  // open: clr
  Register #(.width(32)) register_14 (.D(Write_Data), .en(x13), .clk(clk), .Q(o13));  // open: clr
  Register #(.width(32)) register_15 (.D(Write_Data), .en(x14), .clk(clk), .Q(o14));  // open: clr
  Register #(.width(32)) register_16 (.D(Write_Data), .en(x15), .clk(clk), .Q(o15));  // open: clr
  Register #(.width(32)) register_17 (.D(Write_Data), .en(x16), .clk(clk), .Q(o16));  // open: clr
  Register #(.width(32)) register_18 (.D(Write_Data), .en(x17), .clk(clk), .Q(o17));  // open: clr
  Register #(.width(32)) register_19 (.D(Write_Data), .en(x18), .clk(clk), .Q(o18));  // open: clr
  Register #(.width(32)) register_20 (.D(Write_Data), .en(x19), .clk(clk), .Q(o19));  // open: clr
  Register #(.width(32)) register_21 (.D(Write_Data), .en(x20), .clk(clk), .Q(o20));  // open: clr
  Register #(.width(32)) register_22 (.D(Write_Data), .en(x21), .clk(clk), .Q(o21));  // open: clr
  Register #(.width(32)) register_23 (.D(Write_Data), .en(x22), .clk(clk), .Q(o22));  // open: clr
  Register #(.width(32)) register_24 (.D(Write_Data), .en(x23), .clk(clk), .Q(o23));  // open: clr
  Register #(.width(32)) register_25 (.D(Write_Data), .en(x24), .clk(clk), .Q(o24));  // open: clr
  Register #(.width(32)) register_26 (.D(Write_Data), .en(x25), .clk(clk), .Q(o25));  // open: clr
  Register #(.width(32)) register_27 (.D(Write_Data), .en(x26), .clk(clk), .Q(o26));  // open: clr
  Register #(.width(32)) register_28 (.D(Write_Data), .en(x27), .clk(clk), .Q(o27));  // open: clr
  Register #(.width(32)) register_29 (.D(Write_Data), .en(x28), .clk(clk), .Q(o28));  // open: clr
  Register #(.width(32)) register_30 (.D(Write_Data), .en(x29), .clk(clk), .Q(o29));  // open: clr
  Register #(.width(32)) register_31 (.D(Write_Data), .en(x30), .clk(clk), .Q(o30));  // open: clr
  Register #(.width(32)) register_32 (.D(Write_Data), .en(x31), .clk(clk), .Q(o31));  // open: clr
  Demultiplexer #(.enable("false"), .select(5)) demultiplexer_1 (
    .out1(x1), .out2(x2), .out3(x3), .out4(x4), .out5(x5), .out6(x6), .out7(x7), .out8(x8), .out9(x9),
    .out10(x10), .out11(x11), .out12(x12), .out13(x13), .out14(x14), .out15(x15), .out16(x16), .out17(x17),
    .out18(x18), .out19(x19), .out20(x20), .out21(x21), .out22(x22), .out23(x23), .out24(x24), .out25(x25),
    .out26(x26), .out27(x27), .out28(x28), .out29(x29), .out30(x30), .out31(x31), .in(RegWEn), .sel(rd));  // open: out0
  Multiplexer #(.enable("false"), .select(5), .width(32)) multiplexer_1 (
    .in0(o0), .in1(ra), .in2(sp), .in3(o3), .in4(o4), .in5(t0), .in6(t1), .in7(t2), .in8(s0), .in9(s1),
    .in10(a0), .in11(o11), .in12(o12), .in13(o13), .in14(o14), .in15(o15), .in16(o16), .in17(o17),
    .in18(o18), .in19(o19), .in20(o20), .in21(o21), .in22(o22), .in23(o23), .in24(o24), .in25(o25),
    .in26(o26), .in27(o27), .in28(o28), .in29(o29), .in30(o30), .in31(o31), .out(Read_Data_1), .sel(rs1));
  Multiplexer #(.enable("false"), .select(5), .width(32)) multiplexer_2 (
    .in0(o0), .in1(ra), .in2(sp), .in3(o3), .in4(o4), .in5(t0), .in6(t1), .in7(t2), .in8(s0), .in9(s1),
    .in10(a0), .in11(o11), .in12(o12), .in13(o13), .in14(o14), .in15(o15), .in16(o16), .in17(o17),
    .in18(o18), .in19(o19), .in20(o20), .in21(o21), .in22(o22), .in23(o23), .in24(o24), .in25(o25),
    .in26(o26), .in27(o27), .in28(o28), .in29(o29), .in30(o30), .in31(o31), .out(Read_Data_2), .sel(rs2));

  // Other names for the same wires on the sheet: o1[31:0] = ra; o2[31:0] = sp; o5[31:0] = t0; o6[31:0] = t1;
  //   o7[31:0] = t2; o8[31:0] = s0; o9[31:0] = s1; o10[31:0] = a0; read_data1[31:0] = Read_Data_1;
  //   read_data2[31:0] = Read_Data_2; read_reg1[4:0] = rs1; read_reg2[4:0] = rs2; write_en = RegWEn;
  //   write_reg[4:0] = rd

  // Notes on the sheet:
  //   INPUTS to your circuit
  //   DON'T CHANGE THE LOCATIONS OF THE INPUTS AND OUTPUTS!
  //   These are DEBUG/TEST outputs from your circuit.
  //   OUTPUTS from your circuit
endmodule
